// Logisim project hw2.circ as structural Verilog: 1 circuit, main circuit main
module main (
  input  Clock
);

  wire button_1_out, decoder_1_out0, decoder_1_out1, decoder_1_out2, decoder_1_out3;
  wire [3:0] rom_1_data_2;
  wire [7:0] adder_1_out, adder_2_out, multiplexer_2_out, multiplexer_3_out, register_1_q, register_2_q,
       register_3_q, register_4_q, subtractor_1_out, undriven_2, undriven_3, undriven_4;
  wire [7:4] undriven;
  wire [11:0] rom_1_data;

  Button button_1 (.out(button_1_out));
  // Probe on adder_1_out
  Decoder #(.select(2), .disabled(0)) decoder_1 (
    .out0(decoder_1_out0), .out1(decoder_1_out1), .out2(decoder_1_out2), .out3(decoder_1_out3),
    .sel(rom_1_data_2[1:0]), .en(Clock));
  Register #(.trigger("falling")) register_1 (
    .D(adder_1_out), .Q(register_1_q), .clk(Clock), .clr(button_1_out));  // open: en
  // Probe on rom_1_data_2
  LED led_1 (.in(button_1_out));
  Adder adder_1 (.a(8'h1), .b(register_1_q), .out(adder_1_out));  // open: cin, cout
  // Probe on register_1_q
  // Probe on {undriven, rom_1_data[7:4]}
  // Probe on rom_1_data[11:8]
  Register register_2 (.D(multiplexer_3_out), .Q(register_2_q), .clk(decoder_1_out1), .clr(button_1_out));  // open: en
  Register register_3 (.D(multiplexer_3_out), .Q(register_3_q), .clk(decoder_1_out2), .clr(button_1_out));  // open: en
  Register register_4 (.D(multiplexer_3_out), .Q(register_4_q), .clk(decoder_1_out3), .clr(button_1_out));  // open: en
  ROM #(.dataWidth(16)) rom_1 (.addr(register_1_q), .data({rom_1_data_2, rom_1_data}));  // open: sel
  // Probe on {rom_1_data_2, rom_1_data}
  Multiplexer #(.select(2), .width(8), .enable("false")) multiplexer_1 (
    .in0({undriven, rom_1_data[7:4]}), .in1(register_2_q), .in2(register_3_q), .in3(register_4_q));  // open: out, sel
  Multiplexer #(.select(2), .width(8), .enable("false")) multiplexer_2 (
    .in0(register_2_q), .in1(register_3_q), .in2(register_4_q), .in3(multiplexer_3_out),
    .out(multiplexer_2_out), .sel(rom_1_data[9:8]));
  // Probe on rom_1_data[3:0]
  // Probe on multiplexer_2_out
  Adder adder_2 (.a(undriven_4), .b(multiplexer_2_out), .out(adder_2_out));  // open: cin, cout
  // Probe on adder_2_out
  Subtractor subtractor_1 (.a(multiplexer_2_out), .b(undriven_2), .out(subtractor_1_out));  // open: bin, bout
  // Probe on subtractor_1_out
  Multiplexer #(.select(2), .width(8), .enable("false")) multiplexer_3 (
    .in0(adder_2_out), .in1(subtractor_1_out), .in2(undriven_3), .out(multiplexer_3_out),
    .sel(rom_1_data[1:0]));  // open: in3
  // Probe on multiplexer_3_out
  // Pins of 2 and 4 bits meet at rom_1_data[3:0]
  // Pins of 4 and 8 bits meet at {undriven, rom_1_data[7:4]}
  // Pins of 2 and 4 bits meet at rom_1_data[11:8]
  // Pins of 2 and 4 bits meet at rom_1_data_2

  // Notes on the sheet:
  //   RESET
  //   Program Counter
  //   Output Select
  //   Output Reg
  //   Stored Program
  //   Loaded Instruction
  //   Constant
  //   r0
  //   r1
  //   Register File
  //   contents of rom_1 (hex, n*v repeats v):
  //   1 601 404
  //   Input Reg
  //   Operation
  //   Output Bus
  //   Arithmetic
endmodule
